// Logisim project test.circ as structural Verilog: 1 circuit, main circuit main
module main (
  input  [15:0] in_1,
  input  [15:0] in_2
);

  wire adder16_1_p3, button_1_out, button_2_out, test_1_p2, test_2_p2;

  Button button_1 (.out(button_1_out));
  // test test_1: pin names not known; wires that end beside it: button_1_out, test_1_p2
  // Probe on test_1_p2
  Button button_2 (.out(button_2_out));
  // test test_2: pin names not known; wires that end beside it: button_2_out, test_2_p2
  // Probe on test_2_p2
  // Probe on in_2
  // adder16 adder16_1: pin names not known; wires that end beside it: in_1, in_2, adder16_1_p3, adder16_1_p3, adder16_1_p3
  // Probe on adder16_1_p3
  // Probe on in_1
  // Probe on adder16_1_p3
endmodule
